# Fritzing sketch ArduinoRS (saved by Fritzing 0.9.2b)
breadboards: 1

parts:
  Part1 = Arduino Nano (Rev3.0)
  Flywheel = Trimmer Potentiometer [maximum_resistance=10kΩ package=THT]
  Pusher = Trimmer Potentiometer [maximum_resistance=10kΩ package=THT]
  GLCD_128x1 = 128 x 64 Graphic LCD
  Rev_Trigger = Pushbutton [package=THT]
  Fire_Trigger = Pushbutton [package=THT]
  Flywheel_bottom = DC Motor
  Flywheel_top = DC Motor
  Pusher_Motor = DC Motor
  R2 = Resistor [tolerance=±5% resistance=10k package="0603 [SMD]"]  # not connected
  R3 = Resistor [tolerance=±5% resistance=10k package="0603 [SMD]"]  # not connected
  R4 = Resistor [tolerance=±5% resistance=10k package="0603 [SMD]"]  # not connected
  Dart_Sensor = TSOP312.., 314.. [package=THT]
  Dart_Sensor_LED = LTE-302 [package=lte-302]
  Jam_Door = Pushbutton [package=THT]
  Pusher_return = Pushbutton [package=THT]
  11_1V_2200mAh = LIPO-2000mAh [package=lipo-2000]
  Flywheel_MOSFET = Basic FET N-Channel [package="TO220 [THT]"]
  Pusher_MOSFET = Basic FET N-Channel [package="TO220 [THT]"]
  Magazine_sensor = Pushbutton [package=THT]
  LED_Strip_Left = smd LED [color="Red (633nm)" package="0805 [SMD]"]
  Led_Strip_Right = smd LED [color="Red (633nm)" package="0805 [SMD]"]

nets:
  GND: Part1.GND, Flywheel.leg1, Pusher.leg1, GLCD_128x1.1_Vss, Rev_Trigger.leg1, Fire_Trigger.leg1, Flywheel_bottom.pin_2, Flywheel_top.pin_2, Pusher_Motor.pin_2, Dart_Sensor.GND, Dart_Sensor_LED.A, Jam_Door.leg1, Pusher_return.leg1, 11_1V_2200mAh.-, Magazine_sensor.leg1
  N1: Part1.D2, Rev_Trigger.leg0
  N2: Part1.D3, Fire_Trigger.leg0
  N3: Part1.D4, Jam_Door.leg0
  N4: Part1.D5, Pusher_return.leg0
  N5: Part1.D6, Dart_Sensor.Data
  N6: Part1.D7, Magazine_sensor.leg0
  N7: Part1.D9, GLCD_128x1.7_DB0
  N8: Part1.D10, GLCD_128x1.8_DB1
  N9: Part1.D11/MOSI, GLCD_128x1.9_BD2
  N10: Part1.D12/MISO, GLCD_128x1.15_CS1
  N11: Part1.VIN, 11_1V_2200mAh.+, Flywheel_MOSFET.source, Pusher_MOSFET.source, LED_Strip_Left.cathode, LED_Strip_Left.anode, Led_Strip_Right.cathode, Led_Strip_Right.anode
  N12: Part1.5V, Flywheel.leg2, Pusher.leg2, GLCD_128x1.2_Vdd, Dart_Sensor.Vs, Dart_Sensor_LED.C
  N13: Part1.A7, Pusher_MOSFET.gate
  N14: Part1.A6, Flywheel_MOSFET.gate
  N15: Part1.A1, Pusher.wiper
  N16: Part1.A0, Flywheel.wiper
  N17: Flywheel_bottom.pin_1, Flywheel_top.pin_1, Flywheel_MOSFET.drain
  N18: Pusher_Motor.pin_1, Pusher_MOSFET.drain
