# Fritzing sketch MultiButton (saved by Fritzing 0.9.2b)
circuit board: 5.64444cm x 8.46667cm
breadboards: 1

parts:
  Switch2 = Pushbutton [package=THT]
  Switch5 = Pushbutton [package=THT]
  Switch1 = Pushbutton [package=THT]
  Switch4 = Pushbutton [package=THT]
  Switch3 = Pushbutton [package=THT]
  2500 = Resistor [tolerance=±5% resistance=2.5k package=THT]
  1k = Resistor [tolerance=±5% resistance=1k package=THT]
  5_8k = Resistor [tolerance=±5% resistance=5.8k package=THT]
  10k = Resistor [tolerance=±5% resistance=10k package=THT]
  18k = Resistor [tolerance=±5% resistance=18k package=THT]
  100k = Resistor [tolerance=±5% resistance=100k package=THT]
  VCC1 = Battery
  LED1 = LED - 5mm [color="Red (633nm)" package="5 mm [THT]"]

nets:
  N1: Switch2.leg0, 2500.Pin_0
  N2: Switch2.leg1, Switch5.leg1, Switch1.leg1, Switch4.leg1, Switch3.leg1, VCC1.-
  N3: Switch5.leg0, 18k.Pin_0
  N4: Switch1.leg0, 1k.Pin_0
  N5: Switch4.leg0, 10k.Pin_0
  N6: Switch3.leg0, 5_8k.Pin_0
  N7: 2500.Pin_1, 1k.Pin_1, 5_8k.Pin_1, 10k.Pin_1, 18k.Pin_1, 100k.Pin_0
  N8: 100k.Pin_1, LED1.cathode
  N9: VCC1.+, LED1.anode
