# Fritzing sketch NB-21-X (saved by Fritzing 0.9.2b)
breadboards: 1

parts:
  Part1 = Arduino Nano (Rev3.0) (ICSP)
  BAT1 = BC9VPC [package=bc9vpc]
  Fly = Basic FET N-Channel [package="DPak [SMD]"]
  Push = Basic FET N-Channel [package="DPak [SMD]"]
  Brake = Basic FET N-Channel [package="DPak [SMD]"]
  LED = Basic FET N-Channel [package="DPak [SMD]"]
  S1 = Pushbutton [package=THT]
  S2 = Pushbutton [package=THT]
  S3 = Pushbutton [package=THT]
  S4 = Pushbutton [package=THT]
  S5 = Pushbutton [package=THT]
  S6 = Pushbutton [package=THT]
  S7 = Pushbutton [package=THT]
  S8 = Pushbutton [package=THT]
  R1 = Resistor [tolerance=±5% resistance=10k package="0603 [SMD]"]
  R2 = Resistor [tolerance=±5% resistance=10k package="0603 [SMD]"]
  R3 = Resistor [tolerance=±5% resistance=10k package="0603 [SMD]"]
  R4 = Resistor [tolerance=±5% resistance=10k package="0603 [SMD]"]
  U1 = LCD-16X2 [package=lcd-8x2]
  U2 = Voltage Regulator - 5V [package="DPak [SMD]"]
  100 = Capacitor [package=cap-pth-small2]
  330 = Capacitor Polarized [package=panasonic_c]

nets:
  N1: Part1.D1/TX, S3.leg1
  N2: Part1.D0/RX, S2.leg1
  GND: Part1.GND, BAT1.V-, S1.leg0, S2.leg0, S3.leg0, S4.leg0, S5.leg0, S6.leg0, S7.leg0, S8.leg0, U2.GND, 100.1, 330.+
  N3: Part1.D2, S1.leg1
  N4: Part1.D3, R1.Pin_1
  N5: Part1.D4, S4.leg1
  N6: Part1.D5, R2.Pin_1
  N7: Part1.D6, R3.Pin_1
  N8: Part1.D7, S5.leg1
  N9: Part1.D8, S6.leg1
  N10: Part1.D9, U1.RS
  N11: Part1.D10, U1.E
  N12: Part1.D11/MOSI, U1.DB1
  N13: Part1.D12/MISO, U1.DB3
  N14: Part1.5V, U2.output_voltage, 100.2
  N15: Part1.A2, R4.Pin_1
  N16: Part1.A1, S8.leg1
  N17: Part1.A0, S7.leg1
  N18: Part1.D13/SCK, U1.DB5
  N19: BAT1.V+, U2.input_voltage, 330.-
  N20: Fly.Gate, R1.Pin_0
  N21: Push.Gate, R2.Pin_0
  N22: Brake.Gate, R3.Pin_0
  N23: LED.Gate, R4.Pin_0
