# Fritzing sketch SimpleRS (saved by Fritzing 0.9.2b)
breadboards: 1

parts:
  Part1 = Arduino Nano (Rev3.0)
  SSD1306_7_pin = 128 x 64 Graphic LCD
  Rev_Trigger = Pushbutton [package=THT]
  Fire_Trigger = Pushbutton [package=THT]
  Flywheel_bottom = DC Motor
  Pusher_Motor = DC Motor
  Pusher_return = Pushbutton [package=THT]
  11_1V_2200mAh = LIPO-2000mAh [package=lipo-2000]
  Flywheel_MOSFET = Basic FET N-Channel [package="TO220 [THT]"]
  Pusher_MOSFET = Basic FET N-Channel [package="TO220 [THT]"]
  Flywheel_top = DC Motor
  R1 = Resistor [tolerance=±1% resistance=10k package=THT]  # not connected
  R2 = Resistor [tolerance=±1% resistance=10k package=THT]  # not connected
  R3 = Resistor [tolerance=±1% resistance=10k package=THT]  # not connected

nets:
  N1: Part1.GND, SSD1306_7_pin.1_Vss, Rev_Trigger.leg1, Fire_Trigger.leg1, Flywheel_bottom.pin_2, Pusher_Motor.pin_2, Pusher_return.leg1, 11_1V_2200mAh.-, Flywheel_top.pin_2
  N2: Part1.D2, Pusher_return.leg0
  N3: Part1.D3, Rev_Trigger.leg0
  N4: Part1.D4, Fire_Trigger.leg0
  N5: Part1.D9, SSD1306_7_pin.7_DB0
  N6: Part1.D10, SSD1306_7_pin.8_DB1
  N7: Part1.D11/MOSI, SSD1306_7_pin.9_BD2
  N8: Part1.D12/MISO, SSD1306_7_pin.15_CS1
  N9: Part1.VIN, 11_1V_2200mAh.+, Flywheel_MOSFET.source, Pusher_MOSFET.source
  N10: Part1.5V, SSD1306_7_pin.2_Vdd
  N11: Part1.A7, Pusher_MOSFET.gate
  N12: Part1.A6, Flywheel_MOSFET.gate
  N13: Part1.D13/SCK, SSD1306_7_pin.10_DB3
  N14: Flywheel_bottom.pin_1, Flywheel_MOSFET.drain, Flywheel_top.pin_1
  N15: Pusher_Motor.pin_1, Pusher_MOSFET.drain
