# Fritzing sketch motor-brake (saved by Fritzing 0.9.2b)
breadboards: 1

parts:
  Part1 = Arduino Nano (Rev3.0) (ICSP)
  R1 = Resistor [tolerance=±5% resistance=1k package="0402 [SMD]"]
  R2 = Resistor [tolerance=±5% resistance=1k package="0402 [SMD]"]
  Q1 = Basic FET N-Channel [package="DPak [SMD]"]
  Q2 = Basic FET N-Channel [package="DPak [SMD]"]
  M1 = DC Motor
  D1 = Schottky Diode [part_number=1N5817 package="Melf DO-213 AB [SMD]"]
  D2 = Schottky Diode [part_number=1N5817 package="Melf DO-213 AB [SMD]"]
  12v = BC9VPC [package=bc9vpc]

nets:
  N1: Part1.GND, Q1.source, Q2.source, D1.anode, D2.anode, 12v.V-
  N2: Part1.D3, R1.Pin_0
  N3: Part1.D5, R2.Pin_0
  N4: Part1.VIN, Q1.drain, Q2.drain, M1.pin_1, M1.pin_2, D1.cathode, D2.cathode, 12v.V+
  N5: R1.Pin_1, Q1.Gate
  N6: R2.Pin_1, Q2.Gate
